# Fritzing sketch water monitor (saved by Fritzing 1.0.6)

parts:
  M1 = DOIT Esp32 DevKit v1 (30 pins long, 11 pins width) [part_number=ESP32S-PIN30]
  microSD1 = MicroSD Card Module
  RTC1 = DS3231 AT24C32 Real Time Clock
  GY-NEO6MV1 = GY-NEO6MV2
  A1 = tds-sensor-meter-v1.0_1
  DS1 = DS18B20 1-Wire Temperature Sensor Probe
  M2 = PH meter with sensor in breadboard [package=THT]
  A2 = PH meter
  Part1 = INMP441

nets:
  N1: M1.D2, GY-NEO6MV1.Rx
  N2: M1.D4, GY-NEO6MV1.Tx
  N3: M1.RX2, DS1.DQ, Part1.SCK
  N4: M1.TX2, Part1.WS
  N5: M1.D5, microSD1.CS
  N6: M1.D18, microSD1.SCK
  N7: M1.D19, microSD1.MISO
  N8: M1.D21, RTC1.SDA
  N9: M1.D22, RTC1.SCL
  N10: M1.D23, microSD1.MOSI
  N11: M1.D34, Part1.SD
  N12: M1.D35, M2.pin1
  N13: M1.D32, A2.pin3
  N14: M1.D33, A1.pin1

custom parts:
  DOIT Esp32 DevKit v1 (30 pins long, 11 pins width): The DOIT Esp32 DevKit v1 is one of the development board created by DOIT to evaluate the ESP-WROOM-32 module. It is based on the ESP32 microcontroller that boasts Wifi, Bluetooth, Ethernet and Low Power support all in a single chip. (vanepp) made breadboard work, adjusted pin numbering and labels and reduced size of schematic and cleaned up pcb. This chip is 30pins long (2 x15) and 11 pins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
  MicroSD Card Module: A common microSD card module.
  DS3231 AT24C32 Real Time Clock: Real-time clock basedo on chip DS3231, plus memory chip AT24C32 (32 Kb storage capacity). On-chip temperature sensor with an accuracy of ±3 ℃, I2C bus interface maximum speed: 400 kHz. Operating voltage: 3.3 V to 5.5 V with battery backup capabilities.
  GY-NEO6MV2: Description: Module GPS , type GY-NEO6MV2, pour arduino et autres micro-contrôleurs. Caractéristiques De type GY-NEO6MV2 Alimentation 3V-5V Avec Flight Control EEPROM MWC Antenne large céramique, fort signal, 25 x 25 mm Paramètres de configuration sauvegardés en EEPROM Avec batterie de backup de données LED témoin de signal Module miniaturisé 25 x 35 mm Trou de fixation de 3mm Baud rate par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
  : TDS Meter V1.0 Development Board Water Meter Filter Measuring Water Sensor Module.
  PH meter with sensor in breadboard: DFrobot PH meter (SKU SEN0161)
  PH meter: DFrobot Dissolved Oxygen meter (SKU SEN0237A)
  INMP441: This is a simple breakout board for the INMP441 I2S MEMS microphone.
